// Logisim project tamagotchi 2025 (2).circ as structural Verilog: 11 circuits, main circuit main
module \seleção  (
  input  Enable,
  input  selecionar,
  output out_3,
  output out_4,
  output out_5,
  output out_6,
  output out_7,
  output out_8
);

  wire demultiplexer_1_out6, demultiplexer_1_out7;
  wire [2:0] counter_1_q;

  Counter #(.width(3), .max('h5)) counter_1 (
    .D(3'b001), .count(1'b1), .Q(counter_1_q), .clk(selecionar));  // open: load, carry, clr
  Demultiplexer #(.select(3)) demultiplexer_1 (
    .out0(out_3), .out1(out_4), .out2(out_5), .out3(out_6), .out4(out_7), .out5(out_8),
    .out6(demultiplexer_1_out6), .out7(demultiplexer_1_out7), .in(Enable), .sel(counter_1_q), .en(1'b1));
endmodule

module Contador_decrescente (
  input  in_1,
  input  in_2,
  input  in_3,
  input  in_4,
  input  in_5,
  input  in_6,
  input  in_7,
  input  in_8,
  input  in_9,
  input  in_10,
  output [5:0] out_11,
  output out_12,
  output [5:0] out_13,
  output [5:0] out_14,
  output [5:0] out_15,
  output [5:0] out_16,
  output [5:0] out_17,
  output [5:0] out_18
);

  wire and_1_out, and_2_out, and_3_out, and_4_out, and_5_out, and_6_out, and_7_out, and_8_out, and_9_out,
       and_10_out, and_11_out, and_12_out, and_13_out, and_14_out, and_15_out, button_1_out, button_2_out,
       button_3_out, button_4_out, button_5_out, button_6_out, clock_1_out, mimir_1_out_4, mimir_1_out_5,
       not_1_out, not_2_out, not_3_out, not_4_out, or_1_out, or_2_out, or_3_out, or_4_out,
       \remédio_1_out_11 , s_r_ff_1_q, \seleção_1_out_3 , \seleção_1_out_4 , \seleção_1_out_5 ,
       \seleção_1_out_6 , \seleção_1_out_7 , \seleção_1_out_8 , \seleção_2_out_3 , \seleção_2_out_4 ,
       \seleção_2_out_5 , \seleção_2_out_6 , \seleção_2_out_7 , \seleção_2_out_8 , \seleção_3_out_3 ,
       \seleção_3_out_4 , \seleção_3_out_5 , \seleção_3_out_6 , \seleção_3_out_7 , \seleção_3_out_8 ,
       t_ff_1_qn, t_ff_2_qn, t_ff_3_qn, t_ff_4_qn, t_ff_5_qn, \teste_funções_2_out_10 ,
       \teste_funções_3_out_10 , \teste_funções_4_out_10 ;

  Button button_1 (.out(button_1_out));
  Button button_2 (.out(button_2_out));
  Button button_3 (.out(button_3_out));
  \seleção  \seleção_1  (
    .Enable(in_9), .selecionar(button_1_out), .out_3(\seleção_1_out_3 ), .out_4(\seleção_1_out_4 ),
    .out_5(\seleção_1_out_5 ), .out_6(\seleção_1_out_6 ), .out_7(\seleção_1_out_7 ), .out_8(\seleção_1_out_8 ));
  and and_1 (and_1_out, button_2_out, not_1_out);
  // teste_funções teste_funções_1: pin names not known; wires that end beside it: button_3_out, in_2, in_3, in_4, out_11[0], out_11[1], out_11[2], out_11[3], out_11[4], out_11[5]
  \seleção  \seleção_2  (
    .Enable(in_1), .selecionar(button_4_out), .out_3(\seleção_2_out_3 ), .out_4(\seleção_2_out_4 ),
    .out_5(\seleção_2_out_5 ), .out_6(\seleção_2_out_6 ), .out_7(\seleção_2_out_7 ), .out_8(\seleção_2_out_8 ));
  Button button_4 (.out(button_4_out));
  T_Flip_Flop t_ff_1 (.clk(in_5), .T(1'b1), .Qn(t_ff_1_qn), .preset(in_6));  // open: Q, reset, en
  Button button_5 (.out(button_5_out));
  and and_2 (and_2_out, \seleção_1_out_3 , and_1_out);
  and and_3 (and_3_out, \seleção_1_out_4 , and_1_out);
  and and_4 (and_4_out, \seleção_1_out_5 , and_1_out);
  and and_5 (and_5_out, \seleção_1_out_6 , and_1_out);
  and and_6 (and_6_out, \seleção_1_out_7 , and_1_out);
  and and_7 (and_7_out, and_1_out, \seleção_1_out_8 );
  Clock clock_1 (.out(clock_1_out));
  not not_1 (not_1_out, and_14_out);
  LED led_1 (.in(\seleção_2_out_3 ));
  LED led_2 (.in(\seleção_2_out_4 ));
  LED led_3 (.in(\seleção_2_out_5 ));
  T_Flip_Flop t_ff_2 (.clk(in_5), .T(t_ff_1_qn), .Qn(t_ff_2_qn), .preset(in_6));  // open: Q, reset, en
  not not_2 (not_2_out, s_r_ff_1_q);
  S_R_Flip_Flop s_r_ff_1 (
    .S(and_7_out), .clk(clock_1_out), .R(mimir_1_out_5), .Q(s_r_ff_1_q));  // open: Qn, preset, reset, en
  LED led_4 (.in(\seleção_2_out_6 ));
  LED led_5 (.in(\seleção_2_out_7 ));
  LED led_6 (.in(\seleção_2_out_8 ));
  and and_8 (and_8_out, t_ff_1_qn, t_ff_2_qn);
  or or_1 (or_1_out, and_12_out, button_5_out);
  LED led_7 (.in(\seleção_3_out_3 ));
  \seleção  \seleção_3  (
    .Enable(\seleção_2_out_3 ), .selecionar(button_6_out), .out_3(\seleção_3_out_3 ),
    .out_4(\seleção_3_out_4 ), .out_5(\seleção_3_out_5 ), .out_6(\seleção_3_out_6 ),
    .out_7(\seleção_3_out_7 ), .out_8(\seleção_3_out_8 ));
  Button button_6 (.out(button_6_out));
  T_Flip_Flop t_ff_3 (.clk(in_5), .T(and_8_out), .Qn(t_ff_3_qn), .preset(in_6));  // open: Q, reset, en
  \teste_funções  \teste_funções_2  (
    .in_1(or_1_out), .in_2(not_2_out), .in_3(and_2_out), .out_4(out_13[0]), .out_5(out_13[1]),
    .out_6(out_13[2]), .out_7(out_13[3]), .out_8(out_13[4]), .out_9(out_13[5]),
    .out_10(\teste_funções_2_out_10 ));
  \teste_funções  \teste_funções_3  (
    .in_1(or_1_out), .in_2(not_2_out), .in_3(and_3_out), .out_4(out_14[0]), .out_5(out_14[1]),
    .out_6(out_14[2]), .out_7(out_14[3]), .out_8(out_14[4]), .out_9(out_14[5]),
    .out_10(\teste_funções_3_out_10 ));
  \teste_funções  \teste_funções_4  (
    .in_1(or_1_out), .in_2(not_2_out), .in_3(and_4_out), .out_4(out_15[0]), .out_5(out_15[1]),
    .out_6(out_15[2]), .out_7(out_15[3]), .out_8(out_15[4]), .out_9(out_15[5]),
    .out_10(\teste_funções_4_out_10 ));
  \teste_funções  \teste_funções_5  (
    .in_1(or_1_out), .in_2(not_2_out), .in_3(and_5_out), .out_4(out_16[0]), .out_5(out_16[1]),
    .out_6(out_16[2]), .out_7(out_16[3]), .out_8(out_16[4]), .out_9(out_16[5]));  // open: out_10
  mimir mimir_1 (
    .in_1(s_r_ff_1_q), .in_2(in_10), .in_3(or_1_out), .out_4(mimir_1_out_4), .out_5(mimir_1_out_5),
    .out_6(out_18[0]), .out_7(out_18[1]), .out_8(out_18[2]), .out_9(out_18[3]), .out_10(out_18[4]),
    .out_11(out_18[5]));
  LED led_8 (.in(\seleção_3_out_4 ));
  LED led_9 (.in(\seleção_3_out_5 ));
  LED led_10 (.in(\seleção_3_out_6 ));
  and and_9 (and_9_out, and_8_out, t_ff_3_qn);
  LED led_11 (.in(\seleção_3_out_7 ));
  LED led_12 (.in(\seleção_3_out_8 ));
  T_Flip_Flop t_ff_4 (.clk(in_5), .T(and_9_out), .Qn(t_ff_4_qn), .preset(in_6));  // open: Q, reset, en
  not not_3 (not_3_out, or_1_out);
  or or_2 (or_2_out, or_3_out, and_11_out);
  or or_3 (or_3_out, \teste_funções_4_out_10 , \teste_funções_3_out_10 , \teste_funções_2_out_10 , mimir_1_out_4);
  and and_10 (and_10_out, and_9_out, t_ff_4_qn);
  and and_11 (and_11_out, not_3_out, or_2_out);
  \remédio  \remédio_1  (
    .in_1(or_1_out), .in_2(and_11_out), .in_3(and_6_out), .out_4(out_17[0]), .out_5(out_17[1]),
    .out_6(out_17[2]), .out_7(out_17[3]), .out_8(out_17[4]), .out_9(out_17[5]), .out_11(\remédio_1_out_11 ));  // open: out_10
  T_Flip_Flop t_ff_5 (.clk(in_5), .T(and_10_out), .Qn(t_ff_5_qn), .preset(in_6));  // open: Q, reset, en
  and and_12 (and_12_out, \remédio_1_out_11 , and_13_out);
  and and_13 (and_13_out, out_17[2], out_17[1], out_17[0], out_17[4], out_17[3], out_17[5]);
  and and_14 (and_14_out, ~out_17[2], ~out_17[1], ~out_17[0], ~out_17[4], ~out_17[3], ~out_17[5]);  // AND_Gate
  and and_15 (and_15_out, and_10_out, t_ff_5_qn);
  T_Flip_Flop t_ff_6 (.clk(in_5), .T(and_15_out), .preset(in_6));  // open: Q, Qn, reset, en
  not not_4 (not_4_out, in_7);
  or or_4 (or_4_out, in_8, out_12);
  and and_16 (out_12, not_4_out, or_4_out);
endmodule

module main (
  input  in_1,
  input  in_2,
  output out_3
);

  wire and_1_out, and_2_out, and_3_out, and_4_out, and_5_out, and_6_out, and_7_out, and_8_out, and_9_out,
       and_10_out, and_11_out, and_12_out, and_13_out, and_14_out, and_15_out, and_16_out, and_17_out,
       and_18_out, and_19_out, and_20_out, and_21_out, and_22_out, and_23_out, and_24_out, and_25_out,
       and_26_out, and_27_out, and_28_out, and_29_out, and_30_out, and_31_out, and_33_out, clock_1_out,
       d_ff_1_q, d_ff_2_q, d_ff_3_q, d_ff_4_q, d_ff_5_q, d_ff_6_q, d_ff_7_q, not_1_out, not_2_out, not_3_out,
       not_4_out, not_5_out, not_6_out, not_7_out, not_8_out, not_9_out, not_10_out, not_11_out, not_12_out,
       not_14_out, or_1_out, or_2_out, or_3_out, or_4_out, or_5_out, or_6_out, or_7_out, or_8_out, or_9_out,
       t_ff_1_qn, t_ff_2_qn, t_ff_3_qn, t_ff_4_qn, t_ff_5_qn, xor_1_out, xor_2_out, xor_3_out, xor_4_out,
       xor_5_out, xor_6_out, xor_7_out, xor_8_out, xor_9_out;
  wire [5:0] t_ff_1_q;

  Clock clock_1 (.out(clock_1_out));
  not not_1 (not_1_out, d_ff_1_q);
  and and_1 (and_1_out, not_14_out, in_2);
  T_Flip_Flop t_ff_1 (
    .clk(clock_1_out), .T(in_1), .Q(t_ff_1_q[0]), .Qn(t_ff_1_qn), .preset(or_1_out), .reset(and_3_out),
    .en(out_3));
  or or_1 (or_1_out, d_ff_7_q, and_2_out);
  and and_2 (and_2_out, d_ff_1_q, and_1_out);
  and and_3 (and_3_out, not_1_out, not_1_out, and_1_out);
  and and_4 (and_4_out, 1'b1, t_ff_1_q[0]);
  D_Flip_Flop d_ff_1 (.clk(and_1_out), .D(xor_1_out), .Q(d_ff_1_q), .en(not_14_out));  // open: Qn, preset, reset
  xor xor_1 (xor_1_out, t_ff_1_q[0], 1'b1);
  T_Flip_Flop t_ff_2 (
    .clk(clock_1_out), .T(t_ff_1_qn), .Q(t_ff_1_q[1]), .Qn(t_ff_2_qn), .preset(or_2_out), .reset(and_6_out),
    .en(out_3));
  or or_2 (or_2_out, d_ff_7_q, and_5_out);
  and and_5 (and_5_out, d_ff_2_q, and_1_out);
  not not_2 (not_2_out, d_ff_2_q);
  and and_6 (and_6_out, not_2_out, not_2_out, and_1_out);
  and and_7 (and_7_out, t_ff_1_qn, t_ff_2_qn);
  or or_3 (or_3_out, d_ff_7_q, and_8_out);
  and and_8 (and_8_out, d_ff_3_q, and_1_out);
  not not_3 (not_3_out, d_ff_3_q);
  xor xor_2 (xor_2_out, 1'b1, and_4_out);
  and and_9 (and_9_out, 1'b1, and_4_out);
  and and_10 (and_10_out, 1'b1, t_ff_1_q[1]);
  and and_11 (and_11_out, t_ff_1_q[1], and_4_out);
  xor xor_3 (xor_3_out, 1'b1, or_5_out);
  and and_12 (and_12_out, 1'b1, or_5_out);
  and and_13 (and_13_out, 1'b1, t_ff_1_q[2]);
  and and_14 (and_14_out, t_ff_1_q[2], or_5_out);
  T_Flip_Flop t_ff_3 (
    .clk(clock_1_out), .T(and_7_out), .Q(t_ff_1_q[2]), .Qn(t_ff_3_qn), .preset(or_3_out), .reset(and_15_out),
    .en(out_3));
  and and_15 (and_15_out, not_3_out, not_3_out, and_1_out);
  and and_16 (and_16_out, and_7_out, t_ff_3_qn);
  or or_4 (or_4_out, d_ff_7_q, and_17_out);
  or or_5 (or_5_out, and_9_out, and_10_out, and_11_out);
  or or_6 (or_6_out, and_12_out, and_13_out, and_14_out);
  T_Flip_Flop t_ff_4 (
    .clk(clock_1_out), .T(and_16_out), .Q(t_ff_1_q[3]), .Qn(t_ff_4_qn), .preset(or_4_out),
    .reset(and_18_out), .en(out_3));
  and and_17 (and_17_out, d_ff_4_q, and_1_out);
  not not_4 (not_4_out, d_ff_4_q);
  and and_18 (and_18_out, not_4_out, not_4_out, and_1_out);
  D_Flip_Flop d_ff_2 (.clk(and_1_out), .D(xor_4_out), .Q(d_ff_2_q), .en(not_14_out));  // open: Qn, preset, reset
  xor xor_4 (xor_4_out, t_ff_1_q[1], xor_2_out);
  xor xor_5 (xor_5_out, t_ff_1_q[2], xor_3_out);
  and and_19 (and_19_out, and_16_out, t_ff_4_qn);
  D_Flip_Flop d_ff_3 (.clk(and_1_out), .D(xor_5_out), .Q(d_ff_3_q), .en(not_14_out));  // open: Qn, preset, reset
  or or_7 (or_7_out, d_ff_7_q, and_20_out);
  T_Flip_Flop t_ff_5 (
    .clk(clock_1_out), .T(and_19_out), .Q(t_ff_1_q[4]), .Qn(t_ff_5_qn), .preset(or_7_out),
    .reset(and_21_out), .en(out_3));
  and and_20 (and_20_out, d_ff_5_q, and_1_out);
  not not_5 (not_5_out, d_ff_5_q);
  and and_21 (and_21_out, not_5_out, not_5_out, and_1_out);
  xor xor_6 (xor_6_out, 1'b1, or_6_out);
  and and_22 (and_22_out, 1'b1, or_6_out);
  and and_23 (and_23_out, 1'b1, t_ff_1_q[3]);
  and and_24 (and_24_out, t_ff_1_q[3], or_6_out);
  or or_8 (or_8_out, d_ff_7_q, and_26_out);
  T_Flip_Flop t_ff_6 (
    .clk(clock_1_out), .T(and_25_out), .Q(t_ff_1_q[5]), .preset(or_8_out), .reset(and_27_out), .en(out_3));  // open: Qn
  and and_25 (and_25_out, and_19_out, t_ff_5_qn);
  and and_26 (and_26_out, d_ff_6_q, and_1_out);
  not not_6 (not_6_out, d_ff_6_q);
  xor xor_7 (xor_7_out, t_ff_1_q[3], xor_6_out);
  or or_9 (or_9_out, and_22_out, and_23_out, and_24_out);
  and and_27 (and_27_out, not_6_out, not_6_out, and_1_out);
  D_Flip_Flop d_ff_4 (.clk(and_1_out), .D(xor_7_out), .Q(d_ff_4_q), .en(not_14_out));  // open: Qn, preset, reset
  // Probe on t_ff_1_q
  and and_28 (and_28_out, t_ff_1_q[5], and_29_out);
  xor xor_8 (xor_8_out, t_ff_1_q[4], or_9_out);
  and and_29 (and_29_out, or_9_out, t_ff_1_q[4]);
  not not_7 (not_7_out, t_ff_1_q[0]);
  not not_8 (not_8_out, t_ff_1_q[1]);
  not not_9 (not_9_out, t_ff_1_q[2]);
  not not_10 (not_10_out, t_ff_1_q[3]);
  not not_11 (not_11_out, t_ff_1_q[4]);
  not not_12 (not_12_out, t_ff_1_q[5]);
  xor xor_9 (xor_9_out, and_29_out, t_ff_1_q[5]);
  D_Flip_Flop d_ff_5 (.clk(and_1_out), .D(xor_8_out), .Q(d_ff_5_q), .en(not_14_out));  // open: Qn, preset, reset
  and and_30 (and_30_out, not_9_out, not_7_out, not_8_out, not_10_out, not_11_out, not_12_out);
  and and_31 (and_31_out, t_ff_1_q[0], t_ff_1_q[1], t_ff_1_q[2], t_ff_1_q[3], t_ff_1_q[5], t_ff_1_q[4]);
  D_Flip_Flop d_ff_6 (.clk(and_1_out), .D(xor_9_out), .Q(d_ff_6_q), .en(not_14_out));  // open: Qn, preset, reset
  not not_13 (out_3, and_30_out);
  // AND_Gate and_32 has open pins: in0=xor_9_out, in1=xor_8_out, in2=xor_7_out, in4=xor_5_out, in5=xor_4_out, in6=xor_1_out, out=open
  and and_33 (and_33_out, and_28_out, and_31_out);
  not not_14 (not_14_out, and_33_out);
  D_Flip_Flop d_ff_7 (.clk(and_1_out), .D(and_28_out), .Q(d_ff_7_q), .reset(and_31_out));  // open: Qn, preset, en
endmodule

module status (
  input  [12:0] in_1,
  input  selecionar,
  input  in_3,
  output [12:0] out_4,
  output [12:0] out_5,
  output [12:0] out_6,
  output [12:0] out_7,
  output [12:0] out_8,
  output [12:0] out_9,
  output [12:0] out_10,
  output [12:0] out_11,
  output [12:0] out_12,
  output [12:0] out_13,
  output [12:0] out_14,
  output [12:0] out_15,
  output [12:0] out_16
);

  wire demultiplexer_1_out4;
  wire [2:0] counter_1_q;
  wire [3:0] demultiplexer_1_out0;
  wire [12:0] rom_1_data, rom_2_data, rom_3_data, rom_4_data, rom_5_data, rom_6_data, rom_7_data, rom_8_data,
       rom_9_data, rom_10_data, rom_11_data, rom_12_data;

  Demultiplexer #(.select(3)) demultiplexer_1 (
    .out0(demultiplexer_1_out0[0]), .out1(demultiplexer_1_out0[1]), .out2(demultiplexer_1_out0[2]),
    .out3(demultiplexer_1_out0[3]), .out4(demultiplexer_1_out4), .in(1'b1), .sel(counter_1_q));  // open: out5, out6, out7, en
  Counter #(.width(3), .max('h4)) counter_1 (
    .D(3'b001), .count(1'b1), .Q(counter_1_q), .clk(selecionar));  // open: load, carry, clr
  ROM #(.addrWidth(4), .dataWidth(13)) rom_1 (.addr(demultiplexer_1_out0), .data(rom_1_data), .sel(in_3));
  ROM #(.addrWidth(4), .dataWidth(13)) rom_2 (.addr(demultiplexer_1_out0), .data(rom_2_data), .sel(in_3));
  ROM #(.addrWidth(4), .dataWidth(13)) rom_3 (.addr(demultiplexer_1_out0), .data(rom_3_data), .sel(in_3));
  ROM #(.addrWidth(4), .dataWidth(13)) rom_4 (.addr(demultiplexer_1_out0), .data(rom_4_data), .sel(in_3));
  ROM #(.addrWidth(4), .dataWidth(13)) rom_5 (.addr(demultiplexer_1_out0), .data(rom_5_data), .sel(in_3));
  ROM #(.addrWidth(4), .dataWidth(13)) rom_6 (.addr(demultiplexer_1_out0), .data(rom_6_data), .sel(in_3));
  ROM #(.addrWidth(4), .dataWidth(13)) rom_7 (.addr(demultiplexer_1_out0), .data(rom_7_data), .sel(in_3));
  ROM #(.addrWidth(4), .dataWidth(13)) rom_8 (.addr(demultiplexer_1_out0), .data(rom_8_data), .sel(in_3));
  ROM #(.addrWidth(4), .dataWidth(13)) rom_9 (.addr(demultiplexer_1_out0), .data(rom_9_data), .sel(in_3));
  ROM #(.addrWidth(4), .dataWidth(13)) rom_10 (.addr(demultiplexer_1_out0), .data(rom_10_data), .sel(in_3));
  DotMatrix #(.matrixcols(13), .matrixrows(13)) dotmatrix_1 (
    .col0(out_4), .col1(out_5), .col2(out_6), .col3(out_7), .col4(out_8), .col5(out_9), .col6(out_10),
    .col7(out_11), .col8(out_12), .col9(out_13), .col10(out_14), .col11(out_15), .col12(out_16));
  assign out_4 = in_3 ? rom_1_data : 13'bz;  // Controlled_Buffer controlled_buffer_1
  assign out_5 = in_3 ? rom_2_data : 13'bz;  // Controlled_Buffer controlled_buffer_2
  assign out_6 = in_3 ? rom_3_data : 13'bz;  // Controlled_Buffer controlled_buffer_3
  assign out_7 = in_3 ? rom_4_data : 13'bz;  // Controlled_Buffer controlled_buffer_4
  assign out_8 = in_3 ? rom_5_data : 13'bz;  // Controlled_Buffer controlled_buffer_5
  assign out_9 = in_3 ? rom_6_data : 13'bz;  // Controlled_Buffer controlled_buffer_6
  assign out_10 = in_3 ? rom_7_data : 13'bz;  // Controlled_Buffer controlled_buffer_7
  assign out_11 = in_3 ? rom_8_data : 13'bz;  // Controlled_Buffer controlled_buffer_8
  assign out_12 = in_3 ? rom_9_data : 13'bz;  // Controlled_Buffer controlled_buffer_9
  assign out_14 = in_3 ? rom_10_data : 13'bz;  // Controlled_Buffer controlled_buffer_10
  assign out_13 = in_3 ? in_1 : 13'bz;  // Controlled_Buffer controlled_buffer_11
  assign out_16 = in_3 ? rom_11_data : 13'bz;  // Controlled_Buffer controlled_buffer_12
  ROM #(.addrWidth(4), .dataWidth(13)) rom_11 (.addr(demultiplexer_1_out0), .data(rom_11_data), .sel(in_3));
  assign out_15 = in_3 ? rom_12_data : 13'bz;  // Controlled_Buffer controlled_buffer_13
  ROM #(.addrWidth(4), .dataWidth(13)) rom_12 (.addr(demultiplexer_1_out0), .data(rom_12_data), .sel(in_3));

  // Notes on the sheet:
  //   contents of rom_1 (hex, n*v repeats v):
  //   260 100 70 0 20 0 0 0 380 1 0 0 4*1
  //   contents of rom_2 (hex, n*v repeats v):
  //   2a0 5e0 b0 0 190 1f 0 0 80 3 0 0 4*1
  //   contents of rom_3 (hex, n*v repeats v):
  //   320 7f8 1f0 1c 10 75 0 0 3f0 3 0 0 4*1
  //   contents of rom_4 (hex, n*v repeats v):
  //   0 5e0 f0 24 190 9b 0 0 80 3 0 0 4*1
  //   contents of rom_5 (hex, n*v repeats v):
  //   0 100 f0 44 20 155 0 0 380 7f 0 0 4*1
  //   contents of rom_6 (hex, n*v repeats v):
  //   0 0 70 54 0 15b 0 0 0 83 0 0 4*1
  //   contents of rom_7 (hex, n*v repeats v):
  //   0 0 0 44 0 115 0 0 0 483 0 0 4*1
  //   contents of rom_8 (hex, n*v repeats v):
  //   7f8 7f8 7f8 54 7f8 15b 0 0 7f8 f83 0 0 4*1
  //   contents of rom_9 (hex, n*v repeats v):
  //   804 804 804 24 804 155 0 0 804 483 0 0 4*1
  //   contents of rom_10 (hex, n*v repeats v):
  //   804 804 804 0 804 75 0 0 804 7f 0 0 4*1
  //   contents of rom_11 (hex, n*v repeats v):
  //   9*0 1 0 0 4*1
  //   contents of rom_12 (hex, n*v repeats v):
  //   7f8 7f8 7f8 0 7f8 1f 0 0 7f8 3 0 0 4*1
endmodule

module tudo (
  input  confirmar,
  input  in_2,
  input  voltar
);

  wire and_1_out, and_2_out, and_3_out, and_4_out, and_5_out, and_6_out, and_7_out, banheiro_out,
       clock_1_out, comida_out, dormir_out, felicidade_out, \funções_mais_lentas_1_out_10 , mimir_1_out_4,
       mimir_1_out_5, not_1_out, not_2_out, not_3_out, not_4_out, not_5_out, or_1_out, or_2_out, or_3_out,
       or_4_out, \remédio_2_out_11 , \remédio_out , reset_out, s_r_ff_1_q, s_r_ff_2_q, selecionar_out,
       \seleção_1_out_3 , \seleção_1_out_4 , \seleção_1_out_5 , \seleção_1_out_6 , \seleção_1_out_7 ,
       \seleção_1_out_8 , status_out, \teste_funções_1_out_10 , \teste_funções_2_out_10 ;
  wire [2:0] counter_1_q;
  wire [9:4] \funções_mais_lentas_1_out_4 , mimir_1_out_6, \remédio_2_out_4 , \teste_funções_1_out_4 ,
       \teste_funções_2_out_4 ;
  wire [12:0] multiplexer_1_out, testes_rom_1_out_5, testes_rom_1_out_6, testes_rom_1_out_7,
       testes_rom_1_out_8, testes_rom_1_out_9, testes_rom_1_out_10, testes_rom_1_out_11, testes_rom_1_out_12,
       testes_rom_1_out_13, testes_rom_1_out_14, testes_rom_1_out_15, testes_rom_1_out_16,
       testes_rom_1_out_17;

  Button selecionar (.out(selecionar_out));
  not not_1 (not_1_out, s_r_ff_2_q);
  \seleção  \seleção_1  (
    .Enable(not_1_out), .selecionar(selecionar_out), .out_3(\seleção_1_out_3 ), .out_4(\seleção_1_out_4 ),
    .out_5(\seleção_1_out_5 ), .out_6(\seleção_1_out_6 ), .out_7(\seleção_1_out_7 ), .out_8(\seleção_1_out_8 ));
  and and_1 (and_1_out, confirmar, not_2_out);
  Button reset (.out(reset_out));
  and comida (comida_out, \seleção_1_out_3 , and_1_out);
  and banheiro (banheiro_out, \seleção_1_out_4 , and_1_out);
  and felicidade (felicidade_out, \seleção_1_out_5 , and_1_out);
  and status (status_out, \seleção_1_out_6 , and_1_out);
  and \remédio  (\remédio_out , \seleção_1_out_7 , and_1_out);
  and dormir (dormir_out, and_1_out, \seleção_1_out_8 );
  Clock clock_1 (.out(clock_1_out));
  not not_2 (not_2_out, and_7_out);
  or or_1 (or_1_out, and_4_out, reset_out);
  not not_3 (not_3_out, s_r_ff_1_q);
  S_R_Flip_Flop s_r_ff_1 (
    .S(dormir_out), .clk(clock_1_out), .R(mimir_1_out_5), .Q(s_r_ff_1_q));  // open: Qn, preset, reset, en
  and and_2 (and_2_out, voltar, s_r_ff_2_q);
  \teste_funções  \teste_funções_1  (
    .in_1(or_1_out), .in_2(not_3_out), .in_3(comida_out), .out_4(\teste_funções_1_out_4 [4]),
    .out_5(\teste_funções_1_out_4 [5]), .out_6(\teste_funções_1_out_4 [6]),
    .out_7(\teste_funções_1_out_4 [7]), .out_8(\teste_funções_1_out_4 [8]),
    .out_9(\teste_funções_1_out_4 [9]), .out_10(\teste_funções_1_out_10 ));
  \funções_mais_lentas  \funções_mais_lentas_1  (
    .in_1(or_1_out), .in_2(not_3_out), .in_3(banheiro_out), .out_4(\funções_mais_lentas_1_out_4 [4]),
    .out_5(\funções_mais_lentas_1_out_4 [5]), .out_6(\funções_mais_lentas_1_out_4 [6]),
    .out_7(\funções_mais_lentas_1_out_4 [7]), .out_8(\funções_mais_lentas_1_out_4 [8]),
    .out_9(\funções_mais_lentas_1_out_4 [9]), .out_10(\funções_mais_lentas_1_out_10 ));
  \teste_funções  \teste_funções_2  (
    .in_1(or_1_out), .in_2(not_3_out), .in_3(felicidade_out), .out_4(\teste_funções_2_out_4 [4]),
    .out_5(\teste_funções_2_out_4 [5]), .out_6(\teste_funções_2_out_4 [6]),
    .out_7(\teste_funções_2_out_4 [7]), .out_8(\teste_funções_2_out_4 [8]),
    .out_9(\teste_funções_2_out_4 [9]), .out_10(\teste_funções_2_out_10 ));
  mimir mimir_1 (
    .in_1(s_r_ff_1_q), .in_2(in_2), .in_3(or_1_out), .out_4(mimir_1_out_4), .out_5(mimir_1_out_5),
    .out_6(mimir_1_out_6[4]), .out_7(mimir_1_out_6[5]), .out_8(mimir_1_out_6[6]), .out_9(mimir_1_out_6[7]),
    .out_10(mimir_1_out_6[8]), .out_11(mimir_1_out_6[9]));
  or or_2 (or_2_out, and_2_out, and_7_out);
  S_R_Flip_Flop s_r_ff_2 (
    .S(status_out), .clk(clock_1_out), .R(or_2_out), .Q(s_r_ff_2_q));  // open: Qn, preset, reset, en
  or or_3 (or_3_out, \teste_funções_2_out_10 , \funções_mais_lentas_1_out_10 , \teste_funções_1_out_10 , mimir_1_out_4);
  not not_4 (not_4_out, s_r_ff_2_q);
  not not_5 (not_5_out, or_1_out);
  or or_4 (or_4_out, or_3_out, and_5_out);
  and and_3 (and_3_out, not_3_out, and_5_out);
  and and_4 (and_4_out, \remédio_2_out_11 , and_6_out);
  and and_5 (and_5_out, not_5_out, or_4_out);
  \remédio  \remédio_2  (
    .in_1(or_1_out), .in_2(and_3_out), .in_3(\remédio_out ), .out_4(\remédio_2_out_4 [4]),
    .out_5(\remédio_2_out_4 [5]), .out_6(\remédio_2_out_4 [6]), .out_7(\remédio_2_out_4 [7]),
    .out_8(\remédio_2_out_4 [8]), .out_9(\remédio_2_out_4 [9]), .out_11(\remédio_2_out_11 ));  // open: out_10
  testes_rom testes_rom_1 (
    .in_1(and_3_out), .in_2(s_r_ff_1_q), .in_3(and_7_out), .in_4(not_4_out), .out_5(testes_rom_1_out_5),
    .out_6(testes_rom_1_out_6), .out_7(testes_rom_1_out_7), .out_8(testes_rom_1_out_8),
    .out_9(testes_rom_1_out_9), .out_10(testes_rom_1_out_10), .out_11(testes_rom_1_out_11),
    .out_12(testes_rom_1_out_12), .out_13(testes_rom_1_out_13), .out_14(testes_rom_1_out_14),
    .out_15(testes_rom_1_out_15), .out_16(testes_rom_1_out_16), .out_17(testes_rom_1_out_17));
  status status_2 (
    .in_3(s_r_ff_2_q), .selecionar(and_1_out), .in_1(multiplexer_1_out), .out_4(testes_rom_1_out_5),
    .out_5(testes_rom_1_out_6), .out_6(testes_rom_1_out_7), .out_7(testes_rom_1_out_8),
    .out_8(testes_rom_1_out_9), .out_9(testes_rom_1_out_10), .out_10(testes_rom_1_out_11),
    .out_11(testes_rom_1_out_12), .out_12(testes_rom_1_out_13), .out_13(testes_rom_1_out_14),
    .out_14(testes_rom_1_out_15), .out_15(testes_rom_1_out_16), .out_16(testes_rom_1_out_17));
  and and_6 (and_6_out, \remédio_2_out_4 [6], \remédio_2_out_4 [5], \remédio_2_out_4 [4], \remédio_2_out_4 [8], \remédio_2_out_4 [7], \remédio_2_out_4 [9]);
  and and_7 (and_7_out, ~\remédio_2_out_4 [6], ~\remédio_2_out_4 [5], ~\remédio_2_out_4 [4], ~\remédio_2_out_4 [8], ~\remédio_2_out_4 [7], ~\remédio_2_out_4 [9]);  // AND_Gate
  DotMatrix #(.matrixcols(13), .matrixrows(13)) dotmatrix_1 (
    .col0(testes_rom_1_out_5), .col1(testes_rom_1_out_6), .col2(testes_rom_1_out_7),
    .col3(testes_rom_1_out_8), .col4(testes_rom_1_out_9), .col5(testes_rom_1_out_10),
    .col6(testes_rom_1_out_11), .col7(testes_rom_1_out_12), .col8(testes_rom_1_out_13),
    .col9(testes_rom_1_out_14), .col10(testes_rom_1_out_15), .col11(testes_rom_1_out_16),
    .col12(testes_rom_1_out_17));
  Counter #(.width(3), .max('h4)) counter_1 (
    .D(3'b001), .count(1'b1), .Q(counter_1_q), .clk(and_1_out));  // open: load, carry, clr
  Multiplexer #(.select(3), .width(13)) multiplexer_1 (
    .in0({3'b010, \remédio_2_out_4 , 4'b0100}), .in1({3'b010, \funções_mais_lentas_1_out_4 , 4'b0100}),
    .in2({3'b010, \teste_funções_2_out_4 , 4'b0100}), .in3({3'b010, \teste_funções_1_out_4 , 4'b0100}),
    .in4({3'b010, mimir_1_out_6, 4'b0100}), .out(multiplexer_1_out), .sel(counter_1_q));  // open: in5, in6, in7, en
endmodule

module \teste_funções  (
  input  in_1,
  input  in_2,
  input  in_3,
  output out_4,
  output out_5,
  output out_6,
  output out_7,
  output out_8,
  output out_9,
  output out_10
);

  wire and_1_out, and_2_out, and_3_out, and_4_out, and_5_out, and_6_out, and_7_out, and_8_out, and_9_out,
       and_10_out, and_11_out, and_12_out, and_13_out, and_14_out, and_15_out, and_16_out, and_17_out,
       and_18_out, and_19_out, and_20_out, and_21_out, and_22_out, and_23_out, and_24_out, and_25_out,
       and_26_out, and_27_out, and_28_out, and_29_out, and_31_out, and_32_out, and_33_out, clock_1_out,
       d_ff_1_q, d_ff_2_q, d_ff_3_q, d_ff_4_q, d_ff_5_q, d_ff_6_q, d_ff_7_q, not_1_out, not_2_out, not_3_out,
       not_4_out, not_5_out, not_6_out, not_7_out, not_8_out, not_9_out, not_10_out, not_11_out, not_12_out,
       not_13_out, not_14_out, or_1_out, or_2_out, or_3_out, or_4_out, or_5_out, or_6_out, or_7_out,
       or_8_out, or_9_out, t_ff_1_qn, t_ff_2_qn, t_ff_3_qn, t_ff_4_qn, t_ff_5_qn, xor_1_out, xor_2_out,
       xor_3_out, xor_4_out, xor_5_out, xor_6_out, xor_7_out, xor_8_out, xor_9_out;

  Clock clock_1 (.out(clock_1_out));
  not not_1 (not_1_out, d_ff_1_q);
  and and_1 (and_1_out, not_14_out, in_3);
  T_Flip_Flop t_ff_1 (
    .clk(clock_1_out), .T(1'b1), .Q(out_4), .Qn(t_ff_1_qn), .preset(or_1_out), .reset(and_3_out),
    .en(and_32_out));
  or or_1 (or_1_out, in_1, d_ff_7_q, and_2_out);
  and and_2 (and_2_out, d_ff_1_q, and_1_out);
  and and_3 (and_3_out, not_1_out, not_1_out, and_1_out);
  and and_4 (and_4_out, 1'b1, out_4);
  D_Flip_Flop d_ff_1 (.clk(and_1_out), .D(xor_1_out), .Q(d_ff_1_q), .en(not_14_out));  // open: Qn, preset, reset
  xor xor_1 (xor_1_out, out_4, 1'b1);
  T_Flip_Flop t_ff_2 (
    .clk(clock_1_out), .T(t_ff_1_qn), .Q(out_5), .Qn(t_ff_2_qn), .preset(or_2_out), .reset(and_6_out),
    .en(and_32_out));
  or or_2 (or_2_out, d_ff_7_q, in_1, and_5_out);
  and and_5 (and_5_out, d_ff_2_q, and_1_out);
  not not_2 (not_2_out, d_ff_2_q);
  and and_6 (and_6_out, not_2_out, not_2_out, and_1_out);
  and and_7 (and_7_out, t_ff_1_qn, t_ff_2_qn);
  or or_3 (or_3_out, d_ff_7_q, and_8_out, in_1);
  and and_8 (and_8_out, d_ff_3_q, and_1_out);
  not not_3 (not_3_out, d_ff_3_q);
  xor xor_2 (xor_2_out, 1'b1, and_4_out);
  and and_9 (and_9_out, 1'b1, and_4_out);
  and and_10 (and_10_out, 1'b1, out_5);
  and and_11 (and_11_out, out_5, and_4_out);
  xor xor_3 (xor_3_out, 1'b1, or_5_out);
  and and_12 (and_12_out, 1'b1, or_5_out);
  and and_13 (and_13_out, 1'b1, out_6);
  and and_14 (and_14_out, out_6, or_5_out);
  T_Flip_Flop t_ff_3 (
    .clk(clock_1_out), .T(and_7_out), .Q(out_6), .Qn(t_ff_3_qn), .preset(or_3_out), .reset(and_15_out),
    .en(and_32_out));
  and and_15 (and_15_out, not_3_out, not_3_out, and_1_out);
  and and_16 (and_16_out, and_7_out, t_ff_3_qn);
  or or_4 (or_4_out, d_ff_7_q, in_1, and_17_out);
  or or_5 (or_5_out, and_9_out, and_10_out, and_11_out);
  or or_6 (or_6_out, and_12_out, and_13_out, and_14_out);
  T_Flip_Flop t_ff_4 (
    .clk(clock_1_out), .T(and_16_out), .Q(out_7), .Qn(t_ff_4_qn), .preset(or_4_out), .reset(and_18_out),
    .en(and_32_out));
  and and_17 (and_17_out, d_ff_4_q, and_1_out);
  not not_4 (not_4_out, d_ff_4_q);
  and and_18 (and_18_out, not_4_out, not_4_out, and_1_out);
  D_Flip_Flop d_ff_2 (.clk(and_1_out), .D(xor_4_out), .Q(d_ff_2_q), .en(not_14_out));  // open: Qn, preset, reset
  xor xor_4 (xor_4_out, out_5, xor_2_out);
  xor xor_5 (xor_5_out, out_6, xor_3_out);
  and and_19 (and_19_out, and_16_out, t_ff_4_qn);
  D_Flip_Flop d_ff_3 (.clk(and_1_out), .D(xor_5_out), .Q(d_ff_3_q), .en(not_14_out));  // open: Qn, preset, reset
  or or_7 (or_7_out, d_ff_7_q, in_1, and_20_out);
  T_Flip_Flop t_ff_5 (
    .clk(clock_1_out), .T(and_19_out), .Q(out_8), .Qn(t_ff_5_qn), .preset(or_7_out), .reset(and_21_out),
    .en(and_32_out));
  and and_20 (and_20_out, d_ff_5_q, and_1_out);
  not not_5 (not_5_out, d_ff_5_q);
  and and_21 (and_21_out, not_5_out, not_5_out, and_1_out);
  xor xor_6 (xor_6_out, 1'b1, or_6_out);
  and and_22 (and_22_out, 1'b1, or_6_out);
  and and_23 (and_23_out, 1'b1, out_7);
  and and_24 (and_24_out, out_7, or_6_out);
  or or_8 (or_8_out, d_ff_7_q, in_1, and_26_out);
  T_Flip_Flop t_ff_6 (
    .clk(clock_1_out), .T(and_25_out), .Q(out_9), .preset(or_8_out), .reset(and_27_out), .en(and_32_out));  // open: Qn
  and and_25 (and_25_out, and_19_out, t_ff_5_qn);
  and and_26 (and_26_out, d_ff_6_q, and_1_out);
  not not_6 (not_6_out, d_ff_6_q);
  xor xor_7 (xor_7_out, out_7, xor_6_out);
  or or_9 (or_9_out, and_22_out, and_23_out, and_24_out);
  and and_27 (and_27_out, not_6_out, not_6_out, and_1_out);
  D_Flip_Flop d_ff_4 (.clk(and_1_out), .D(xor_7_out), .Q(d_ff_4_q), .en(not_14_out));  // open: Qn, preset, reset
  // Probe on {out_9, out_8, out_7, out_6, out_5, out_4}
  and and_28 (and_28_out, out_9, and_29_out);
  xor xor_8 (xor_8_out, out_8, or_9_out);
  and and_29 (and_29_out, or_9_out, out_8);
  not not_7 (not_7_out, out_4);
  not not_8 (not_8_out, out_5);
  not not_9 (not_9_out, out_6);
  not not_10 (not_10_out, out_7);
  not not_11 (not_11_out, out_8);
  not not_12 (not_12_out, out_9);
  xor xor_9 (xor_9_out, and_29_out, out_9);
  D_Flip_Flop d_ff_5 (.clk(and_1_out), .D(xor_8_out), .Q(d_ff_5_q), .en(not_14_out));  // open: Qn, preset, reset
  and and_30 (out_10, not_9_out, not_7_out, not_8_out, not_10_out, not_11_out, not_12_out);
  and and_31 (and_31_out, out_4, out_5, out_6, out_7, out_9, out_8);
  D_Flip_Flop d_ff_6 (.clk(and_1_out), .D(xor_9_out), .Q(d_ff_6_q), .en(not_14_out));  // open: Qn, preset, reset
  and and_32 (and_32_out, in_2, not_13_out);
  not not_13 (not_13_out, out_10);
  and and_33 (and_33_out, and_28_out, and_31_out);
  not not_14 (not_14_out, and_33_out);
  D_Flip_Flop d_ff_7 (.clk(and_1_out), .D(and_28_out), .Q(d_ff_7_q), .reset(and_31_out));  // open: Qn, preset, en
endmodule

module mimir (
  input  in_1,
  input  in_2,
  input  in_3,
  output out_4,
  output out_5,
  output out_6,
  output out_7,
  output out_8,
  output out_9,
  output out_10,
  output out_11
);

  wire and_1_out, and_2_out, and_3_out, and_4_out, and_5_out, and_6_out, and_7_out, and_8_out, and_10_out,
       and_11_out, clock_1_out, not_1_out, not_2_out, or_1_out, or_2_out, or_3_out, or_4_out, or_5_out,
       or_6_out, or_7_out, or_8_out, or_9_out, or_10_out, or_11_out, t_ff_2_qn, t_ff_3_qn, t_ff_4_qn,
       t_ff_5_qn, t_ff_6_qn;

  not not_1 (not_1_out, in_1);
  Clock #(.highDuration(2), .lowDuration(2)) clock_1 (.out(clock_1_out));
  and and_1 (and_1_out, and_3_out, out_10);
  and and_2 (and_2_out, t_ff_2_qn, and_4_out);
  or or_1 (or_1_out, in_3, out_5);
  or or_2 (or_2_out, and_1_out, and_2_out);
  T_Flip_Flop t_ff_1 (
    .clk(clock_1_out), .T(or_2_out), .Q(out_11), .preset(or_1_out), .en(not_2_out));  // open: Qn, reset
  T_Flip_Flop t_ff_2 (
    .clk(clock_1_out), .T(or_4_out), .Q(out_10), .Qn(t_ff_2_qn), .preset(or_3_out), .en(not_2_out));  // open: reset
  or or_3 (or_3_out, in_3, out_5);
  and and_3 (and_3_out, and_5_out, out_9);
  and and_4 (and_4_out, and_6_out, t_ff_3_qn);
  or or_4 (or_4_out, and_3_out, and_4_out);
  or or_5 (or_5_out, in_3, out_5);
  and and_5 (and_5_out, and_7_out, out_8);
  and and_6 (and_6_out, t_ff_4_qn, and_8_out);
  T_Flip_Flop t_ff_3 (
    .clk(clock_1_out), .T(or_6_out), .Q(out_9), .Qn(t_ff_3_qn), .preset(or_5_out), .en(not_2_out));  // open: reset
  or or_6 (or_6_out, and_5_out, and_6_out);
  T_Flip_Flop t_ff_4 (
    .clk(clock_1_out), .T(or_9_out), .Q(out_8), .Qn(t_ff_4_qn), .preset(or_7_out), .en(not_2_out));  // open: reset
  or or_7 (or_7_out, in_3, out_5);
  or or_8 (or_8_out, in_3, out_5);
  and and_7 (and_7_out, out_6, out_7, in_1);
  and and_8 (and_8_out, not_1_out, t_ff_5_qn, t_ff_6_qn);
  T_Flip_Flop t_ff_5 (
    .clk(clock_1_out), .T(or_11_out), .Q(out_7), .Qn(t_ff_5_qn), .preset(or_8_out), .en(not_2_out));  // open: reset
  or or_9 (or_9_out, and_7_out, and_8_out);
  T_Flip_Flop t_ff_6 (
    .clk(clock_1_out), .T(in_2), .Q(out_6), .Qn(t_ff_6_qn), .preset(or_10_out), .en(not_2_out));  // open: reset
  or or_10 (or_10_out, out_5, in_3);
  and and_9 (out_5, out_9, in_1, out_6, out_7, out_8, out_10, out_11);
  and and_10 (and_10_out, out_6, in_1);
  and and_11 (and_11_out, not_1_out, t_ff_6_qn);
  and and_12 (out_4, ~in_1, ~out_9, ~out_6, ~out_7, ~out_8, ~out_10, ~out_11);  // AND_Gate
  or or_11 (or_11_out, and_10_out, and_11_out);
  not not_2 (not_2_out, out_4);
endmodule

module \remédio  (
  input  in_1,
  input  in_2,
  input  in_3,
  output out_4,
  output out_5,
  output out_6,
  output out_7,
  output out_8,
  output out_9,
  output out_10,
  output out_11
);

  wire and_1_out, and_2_out, and_3_out, and_4_out, and_5_out, and_6_out, and_7_out, and_8_out, and_9_out,
       and_10_out, and_11_out, and_12_out, and_13_out, and_14_out, and_15_out, and_16_out, and_17_out,
       and_18_out, and_19_out, and_20_out, and_21_out, and_22_out, and_23_out, and_24_out, and_25_out,
       and_26_out, and_27_out, and_28_out, and_29_out, and_31_out, and_32_out, and_34_out, clock_1_out,
       d_ff_1_q, d_ff_2_q, d_ff_3_q, d_ff_4_q, d_ff_5_q, d_ff_6_q, not_1_out, not_2_out, not_3_out,
       not_4_out, not_5_out, not_6_out, not_7_out, not_8_out, not_9_out, not_10_out, not_11_out, not_12_out,
       not_13_out, not_14_out, or_1_out, or_2_out, or_3_out, or_4_out, or_5_out, or_6_out, or_7_out,
       or_8_out, or_9_out, t_ff_1_qn, t_ff_2_qn, t_ff_3_qn, t_ff_4_qn, t_ff_5_qn, xor_1_out, xor_2_out,
       xor_3_out, xor_4_out, xor_5_out, xor_6_out, xor_7_out, xor_8_out, xor_9_out;

  Clock clock_1 (.out(clock_1_out));
  not not_1 (not_1_out, d_ff_1_q);
  and and_1 (and_1_out, not_14_out, in_3);
  T_Flip_Flop t_ff_1 (
    .clk(clock_1_out), .T(1'b1), .Q(out_4), .Qn(t_ff_1_qn), .preset(or_1_out), .reset(and_3_out),
    .en(and_32_out));
  or or_1 (or_1_out, in_1, out_11, and_2_out);
  and and_2 (and_2_out, d_ff_1_q, and_1_out);
  and and_3 (and_3_out, not_1_out, not_1_out, and_1_out);
  and and_4 (and_4_out, 1'b1, out_4);
  D_Flip_Flop d_ff_1 (.clk(and_1_out), .D(xor_1_out), .Q(d_ff_1_q), .en(not_14_out));  // open: Qn, preset, reset
  xor xor_1 (xor_1_out, out_4, 1'b1);
  T_Flip_Flop t_ff_2 (
    .clk(clock_1_out), .T(t_ff_1_qn), .Q(out_5), .Qn(t_ff_2_qn), .preset(or_2_out), .reset(and_6_out),
    .en(and_32_out));
  or or_2 (or_2_out, out_11, in_1, and_5_out);
  and and_5 (and_5_out, d_ff_2_q, and_1_out);
  not not_2 (not_2_out, d_ff_2_q);
  and and_6 (and_6_out, not_2_out, not_2_out, and_1_out);
  and and_7 (and_7_out, t_ff_1_qn, t_ff_2_qn);
  or or_3 (or_3_out, out_11, and_8_out, in_1);
  and and_8 (and_8_out, d_ff_3_q, and_1_out);
  not not_3 (not_3_out, d_ff_3_q);
  xor xor_2 (xor_2_out, 1'b1, and_4_out);
  and and_9 (and_9_out, 1'b1, and_4_out);
  and and_10 (and_10_out, 1'b1, out_5);
  and and_11 (and_11_out, out_5, and_4_out);
  xor xor_3 (xor_3_out, 1'b1, or_5_out);
  and and_12 (and_12_out, 1'b1, or_5_out);
  and and_13 (and_13_out, 1'b1, out_6);
  and and_14 (and_14_out, out_6, or_5_out);
  T_Flip_Flop t_ff_3 (
    .clk(clock_1_out), .T(and_7_out), .Q(out_6), .Qn(t_ff_3_qn), .preset(or_3_out), .reset(and_15_out),
    .en(and_32_out));
  and and_15 (and_15_out, not_3_out, not_3_out, and_1_out);
  and and_16 (and_16_out, and_7_out, t_ff_3_qn);
  or or_4 (or_4_out, out_11, in_1, and_17_out);
  or or_5 (or_5_out, and_9_out, and_10_out, and_11_out);
  or or_6 (or_6_out, and_12_out, and_13_out, and_14_out);
  T_Flip_Flop t_ff_4 (
    .clk(clock_1_out), .T(and_16_out), .Q(out_7), .Qn(t_ff_4_qn), .preset(or_4_out), .reset(and_18_out),
    .en(and_32_out));
  and and_17 (and_17_out, d_ff_4_q, and_1_out);
  not not_4 (not_4_out, d_ff_4_q);
  and and_18 (and_18_out, not_4_out, not_4_out, and_1_out);
  D_Flip_Flop d_ff_2 (.clk(and_1_out), .D(xor_4_out), .Q(d_ff_2_q), .en(not_14_out));  // open: Qn, preset, reset
  xor xor_4 (xor_4_out, out_5, xor_2_out);
  xor xor_5 (xor_5_out, out_6, xor_3_out);
  and and_19 (and_19_out, and_16_out, t_ff_4_qn);
  D_Flip_Flop d_ff_3 (.clk(and_1_out), .D(xor_5_out), .Q(d_ff_3_q), .en(not_14_out));  // open: Qn, preset, reset
  or or_7 (or_7_out, out_11, in_1, and_20_out);
  T_Flip_Flop t_ff_5 (
    .clk(clock_1_out), .T(and_19_out), .Q(out_8), .Qn(t_ff_5_qn), .preset(or_7_out), .reset(and_21_out),
    .en(and_32_out));
  and and_20 (and_20_out, d_ff_5_q, and_1_out);
  not not_5 (not_5_out, d_ff_5_q);
  and and_21 (and_21_out, not_5_out, not_5_out, and_1_out);
  xor xor_6 (xor_6_out, 1'b1, or_6_out);
  and and_22 (and_22_out, 1'b1, or_6_out);
  and and_23 (and_23_out, 1'b1, out_7);
  and and_24 (and_24_out, out_7, or_6_out);
  or or_8 (or_8_out, out_11, in_1, and_26_out);
  T_Flip_Flop t_ff_6 (
    .clk(clock_1_out), .T(and_25_out), .Q(out_9), .preset(or_8_out), .reset(and_27_out), .en(and_32_out));  // open: Qn
  and and_25 (and_25_out, and_19_out, t_ff_5_qn);
  and and_26 (and_26_out, d_ff_6_q, and_1_out);
  not not_6 (not_6_out, d_ff_6_q);
  xor xor_7 (xor_7_out, out_7, xor_6_out);
  or or_9 (or_9_out, and_22_out, and_23_out, and_24_out);
  and and_27 (and_27_out, not_6_out, not_6_out, and_1_out);
  D_Flip_Flop d_ff_4 (.clk(and_1_out), .D(xor_7_out), .Q(d_ff_4_q), .en(not_14_out));  // open: Qn, preset, reset
  // Probe on {out_9, out_8, out_7, out_6, out_5, out_4}
  and and_28 (and_28_out, out_9, and_29_out);
  xor xor_8 (xor_8_out, out_8, or_9_out);
  and and_29 (and_29_out, or_9_out, out_8);
  not not_7 (not_7_out, out_4);
  not not_8 (not_8_out, out_5);
  not not_9 (not_9_out, out_6);
  not not_10 (not_10_out, out_7);
  not not_11 (not_11_out, out_8);
  not not_12 (not_12_out, out_9);
  xor xor_9 (xor_9_out, and_29_out, out_9);
  D_Flip_Flop d_ff_5 (.clk(and_1_out), .D(xor_8_out), .Q(d_ff_5_q), .en(not_14_out));  // open: Qn, preset, reset
  and and_30 (out_10, not_9_out, not_7_out, not_8_out, not_10_out, not_11_out, not_12_out);
  and and_31 (and_31_out, out_4, out_5, out_6, out_7, out_9, out_8);
  D_Flip_Flop d_ff_6 (.clk(and_1_out), .D(xor_9_out), .Q(d_ff_6_q), .en(not_14_out));  // open: Qn, preset, reset
  and and_32 (and_32_out, in_2, not_13_out);
  not not_13 (not_13_out, out_10);
  // AND_Gate and_33 has open pins: in0=xor_9_out, in1=xor_8_out, in2=xor_7_out, in4=xor_5_out, in5=xor_4_out, in6=xor_1_out, out=open
  and and_34 (and_34_out, and_28_out, and_31_out);
  not not_14 (not_14_out, and_34_out);
  D_Flip_Flop d_ff_7 (.clk(and_1_out), .D(and_28_out), .Q(out_11), .reset(and_31_out));  // open: Qn, preset, en
endmodule

module telas (
  input  in_1,
  input  in_2,
  input  in_3,
  input  [3:0] in_4,
  input  [3:0] in_5,
  input  in_6,
  input  in_7,
  input  in_8,
  input  in_9,
  input  in_10,
  input  in_11,
  input  [3:0] in_12,
  input  [3:0] in_13,
  input  in_14,
  input  [3:0] in_15,
  input  [3:0] in_16,
  input  [3:0] in_17,
  input  [3:0] in_18,
  input  [3:0] in_19,
  input  [3:0] in_20,
  input  [3:0] in_21,
  input  [3:0] in_22,
  input  [3:0] in_23,
  output [12:0] out_24,
  output [12:0] out_25,
  output [12:0] out_26,
  output [12:0] out_27,
  output [12:0] out_28,
  output [12:0] out_29,
  output [12:0] out_30,
  output [12:0] out_31,
  output [12:0] out_32,
  output [12:0] out_33,
  output [12:0] out_34,
  output [12:0] out_35,
  output [12:0] out_36,
  output [12:0] out_37,
  output [12:0] out_38,
  output [12:0] out_39,
  output [12:0] out_40,
  output [12:0] out_41,
  output [12:0] out_42,
  output [12:0] out_43,
  output [12:0] out_44,
  output [12:0] out_45,
  output [12:0] out_46,
  output [12:0] out_47,
  output [12:0] out_48,
  output [12:0] out_49,
  output [12:0] out_50,
  output [12:0] out_51,
  output [12:0] out_52,
  output [12:0] out_53,
  output [12:0] out_54,
  output [12:0] out_55,
  output [12:0] out_56,
  output [12:0] out_57,
  output [12:0] out_58,
  output [12:0] out_59,
  output [12:0] out_60,
  output [12:0] out_61,
  output [12:0] out_62,
  output [12:0] out_63,
  output [12:0] out_64,
  output [12:0] out_65,
  output [12:0] out_66,
  output [12:0] out_67,
  output [12:0] out_68,
  output [12:0] out_69,
  output [12:0] out_70,
  output [12:0] out_71,
  output [12:0] out_72,
  output [12:0] out_73,
  output [12:0] out_74,
  output [12:0] out_75
);

  wire clock_1_out, clock_2_out, clock_3_out, not_1_out;
  wire [1:0] priority_encoder_1_out, priority_encoder_2_out, priority_encoder_3_out;
  wire [3:0] t_ff_1_q, t_ff_2_q, t_ff_3_q;
  wire [12:0] controlled_buffer_1_out, controlled_buffer_2_out, controlled_buffer_3_out,
       controlled_buffer_4_out, controlled_buffer_5_out, controlled_buffer_6_out, controlled_buffer_7_out,
       controlled_buffer_8_out, controlled_buffer_9_out, controlled_buffer_10_out, controlled_buffer_11_out,
       controlled_buffer_12_out, controlled_buffer_13_out, controlled_buffer_19_out,
       controlled_buffer_20_out, controlled_buffer_21_out, controlled_buffer_22_out,
       controlled_buffer_23_out, controlled_buffer_24_out, controlled_buffer_25_out, controlled_buffer_26_out;

  ROM #(.addrWidth(4), .dataWidth(13)) rom_1 (.addr(in_4), .data(out_36));  // open: sel
  ROM #(.addrWidth(4), .dataWidth(13)) rom_2 (.addr(in_5), .data(out_40));  // open: sel
  ROM #(.addrWidth(4), .dataWidth(13)) rom_3 (.addr(in_12), .data(out_41));  // open: sel
  ROM #(.addrWidth(4), .dataWidth(13)) rom_4 (.addr(in_13), .data(out_44));  // open: sel
  ROM #(.addrWidth(4), .dataWidth(13)) rom_5 (.addr(in_15), .data(out_47));  // open: sel
  ROM #(.addrWidth(4), .dataWidth(13)) rom_6 (.addr(in_16), .data(out_50));  // open: sel
  ROM #(.addrWidth(4), .dataWidth(13)) rom_7 (.addr(in_18), .data(out_54));  // open: sel
  ROM #(.addrWidth(4), .dataWidth(13)) rom_8 (.addr(in_19), .data(out_58));  // open: sel
  ROM #(.addrWidth(4), .dataWidth(13)) rom_9 (.addr(in_20), .data(out_62));  // open: sel
  ROM #(.addrWidth(4), .dataWidth(13)) rom_10 (.addr(in_21), .data(out_65));  // open: sel
  ROM #(.addrWidth(4), .dataWidth(13)) rom_11 (.addr(in_23), .data(out_69));  // open: sel
  Clock #(.highDuration(2), .lowDuration(3)) clock_1 (.out(clock_1_out));
  T_Flip_Flop t_ff_1 (.clk(clock_1_out), .T(1'b1), .Q(t_ff_1_q[0]));  // open: Qn, preset, reset, en
  DotMatrix #(.matrixcols(13), .matrixrows(13)) dotmatrix_1 (
    .col0(out_36), .col1(out_40), .col2(out_41), .col3(out_44), .col4(out_47), .col5(out_50), .col6(out_54),
    .col7(out_58), .col8(out_62), .col9(out_65), .col10(out_69), .col11(out_66), .col12(out_52));
  Demultiplexer #(.select(2)) demultiplexer_1 (
    .out1(t_ff_1_q[1]), .out2(t_ff_1_q[2]), .out3(t_ff_1_q[3]), .in(1'b1), .sel(priority_encoder_1_out));  // open: out0, en
  Priority_Encoder #(.select(2), .disabled(0)) priority_encoder_1 (
    .in0(1'b1), .in1(in_1), .in2(in_2), .in3(in_3), .out(priority_encoder_1_out));  // open: gs, en_out, en_in
  ROM #(.addrWidth(4), .dataWidth(13)) rom_12 (.addr(t_ff_1_q), .data(out_24));  // open: sel
  ROM #(.addrWidth(4), .dataWidth(13)) rom_13 (.addr(t_ff_1_q), .data(out_25));  // open: sel
  ROM #(.addrWidth(4), .dataWidth(13)) rom_14 (.addr(t_ff_1_q), .data(out_26));  // open: sel
  ROM #(.addrWidth(4), .dataWidth(13)) rom_15 (.addr(t_ff_1_q), .data(out_27));  // open: sel
  ROM #(.addrWidth(4), .dataWidth(13)) rom_16 (.addr(t_ff_1_q), .data(out_28));  // open: sel
  ROM #(.addrWidth(4), .dataWidth(13)) rom_17 (.addr(t_ff_1_q), .data(out_29));  // open: sel
  ROM #(.addrWidth(4), .dataWidth(13)) rom_18 (.addr(t_ff_1_q), .data(out_31));  // open: sel
  ROM #(.addrWidth(4), .dataWidth(13)) rom_19 (.addr(t_ff_1_q), .data(out_32));  // open: sel
  ROM #(.addrWidth(4), .dataWidth(13)) rom_20 (.addr(t_ff_1_q), .data(out_33));  // open: sel
  ROM #(.addrWidth(4), .dataWidth(13)) rom_21 (.addr(t_ff_1_q), .data(out_34));  // open: sel
  ROM #(.addrWidth(4), .dataWidth(13)) rom_22 (.addr(t_ff_1_q), .data(out_37));  // open: sel
  ROM #(.addrWidth(4), .dataWidth(13)) rom_23 (.addr(in_17), .data(out_52));  // open: sel
  ROM #(.addrWidth(4), .dataWidth(13)) rom_24 (.addr(in_22), .data(out_66));  // open: sel
  Clock #(.highDuration(2), .lowDuration(3)) clock_2 (.out(clock_2_out));
  T_Flip_Flop t_ff_2 (.clk(clock_2_out), .T(1'b1), .Q(t_ff_2_q[0]));  // open: Qn, preset, reset, en
  DotMatrix #(.matrixcols(13), .matrixrows(13)) dotmatrix_2 (
    .col0(out_24), .col1(out_25), .col2(out_26), .col3(out_27), .col4(out_28), .col5(out_29), .col6(out_31),
    .col7(out_32), .col8(out_33), .col9(out_34), .col10(out_37), .col11(out_35), .col12(out_30));
  Demultiplexer #(.select(2)) demultiplexer_2 (
    .out1(t_ff_2_q[1]), .out2(t_ff_2_q[2]), .out3(t_ff_2_q[3]), .in(1'b1), .sel(priority_encoder_2_out));  // open: out0, en
  Priority_Encoder #(.select(2), .disabled(0)) priority_encoder_2 (
    .in0(1'b1), .in1(in_9), .in2(in_10), .in3(in_11), .out(priority_encoder_2_out));  // open: gs, en_out, en_in
  ROM #(.addrWidth(4), .dataWidth(13)) rom_25 (.addr(t_ff_2_q), .data(out_39), .sel(in_14));
  ROM #(.addrWidth(4), .dataWidth(13)) rom_26 (.addr(t_ff_2_q), .data(out_43), .sel(in_14));
  ROM #(.addrWidth(4), .dataWidth(13)) rom_27 (.addr(t_ff_2_q), .data(out_46), .sel(in_14));
  ROM #(.addrWidth(4), .dataWidth(13)) rom_28 (.addr(t_ff_2_q), .data(out_49), .sel(in_14));
  ROM #(.addrWidth(4), .dataWidth(13)) rom_29 (.addr(t_ff_2_q), .data(out_53), .sel(in_14));
  ROM #(.addrWidth(4), .dataWidth(13)) rom_30 (.addr(t_ff_2_q), .data(out_56), .sel(in_14));
  ROM #(.addrWidth(4), .dataWidth(13)) rom_31 (.addr(t_ff_2_q), .data(out_61), .sel(in_14));
  ROM #(.addrWidth(4), .dataWidth(13)) rom_32 (.addr(t_ff_2_q), .data(out_64), .sel(in_14));
  ROM #(.addrWidth(4), .dataWidth(13)) rom_33 (.addr(t_ff_2_q), .data(out_68), .sel(in_14));
  ROM #(.addrWidth(4), .dataWidth(13)) rom_34 (.addr(t_ff_2_q), .data(out_72), .sel(in_14));
  ROM #(.addrWidth(4), .dataWidth(13)) rom_35 (.addr(t_ff_2_q), .data(out_75), .sel(in_14));
  ROM #(.addrWidth(4), .dataWidth(13)) rom_36 (.addr(t_ff_1_q), .data(out_30));  // open: sel
  ROM #(.addrWidth(4), .dataWidth(13)) rom_37 (.addr(t_ff_1_q), .data(out_35));  // open: sel
  assign controlled_buffer_1_out = in_14 ? out_39 : 13'bz;  // Controlled_Buffer controlled_buffer_1
  assign controlled_buffer_2_out = in_14 ? out_43 : 13'bz;  // Controlled_Buffer controlled_buffer_2
  assign controlled_buffer_3_out = in_14 ? out_46 : 13'bz;  // Controlled_Buffer controlled_buffer_3
  assign controlled_buffer_4_out = in_14 ? out_49 : 13'bz;  // Controlled_Buffer controlled_buffer_4
  assign controlled_buffer_5_out = in_14 ? out_53 : 13'bz;  // Controlled_Buffer controlled_buffer_5
  assign controlled_buffer_6_out = in_14 ? out_56 : 13'bz;  // Controlled_Buffer controlled_buffer_6
  assign controlled_buffer_7_out = in_14 ? out_61 : 13'bz;  // Controlled_Buffer controlled_buffer_7
  assign controlled_buffer_8_out = in_14 ? out_64 : 13'bz;  // Controlled_Buffer controlled_buffer_8
  assign controlled_buffer_9_out = in_14 ? out_68 : 13'bz;  // Controlled_Buffer controlled_buffer_9
  assign controlled_buffer_10_out = in_14 ? out_72 : 13'bz;  // Controlled_Buffer controlled_buffer_10
  assign controlled_buffer_11_out = in_14 ? out_75 : 13'bz;  // Controlled_Buffer controlled_buffer_11
  DotMatrix #(.matrixcols(13), .matrixrows(13)) dotmatrix_3 (
    .col0(controlled_buffer_1_out), .col1(controlled_buffer_2_out), .col2(controlled_buffer_3_out),
    .col3(controlled_buffer_4_out), .col4(controlled_buffer_5_out), .col5(controlled_buffer_6_out),
    .col6(controlled_buffer_7_out), .col7(controlled_buffer_8_out), .col8(controlled_buffer_9_out),
    .col9(controlled_buffer_10_out), .col10(controlled_buffer_11_out), .col11(controlled_buffer_12_out),
    .col12(controlled_buffer_13_out));
  assign controlled_buffer_12_out = in_14 ? out_73 : 13'bz;  // Controlled_Buffer controlled_buffer_12
  ROM #(.addrWidth(4), .dataWidth(13)) rom_38 (.addr(t_ff_2_q), .data(out_73), .sel(in_14));
  assign controlled_buffer_13_out = in_14 ? out_59 : 13'bz;  // Controlled_Buffer controlled_buffer_13
  ROM #(.addrWidth(4), .dataWidth(13)) rom_39 (.addr(t_ff_2_q), .data(out_59), .sel(in_14));
  Clock #(.highDuration(2), .lowDuration(3)) clock_3 (.out(clock_3_out));
  T_Flip_Flop t_ff_3 (.clk(clock_3_out), .T(1'b1), .Q(t_ff_3_q[0]));  // open: Qn, preset, reset, en
  not not_1 (not_1_out, in_14);
  Demultiplexer #(.select(2)) demultiplexer_3 (
    .out1(t_ff_3_q[1]), .out2(t_ff_3_q[2]), .out3(t_ff_3_q[3]), .in(1'b1), .sel(priority_encoder_3_out));  // open: out0, en
  Priority_Encoder #(.select(2), .disabled(0)) priority_encoder_3 (
    .in0(1'b1), .in1(in_6), .in2(in_7), .in3(in_8), .out(priority_encoder_3_out));  // open: gs, en_out, en_in
  ROM #(.addrWidth(4), .dataWidth(13)) rom_40 (.addr(t_ff_3_q), .data(out_38), .sel(not_1_out));
  ROM #(.addrWidth(4), .dataWidth(13)) rom_41 (.addr(t_ff_3_q), .data(out_42), .sel(not_1_out));
  ROM #(.addrWidth(4), .dataWidth(13)) rom_42 (.addr(t_ff_3_q), .data(out_45), .sel(not_1_out));
  ROM #(.addrWidth(4), .dataWidth(13)) rom_43 (.addr(t_ff_3_q), .data(out_48), .sel(not_1_out));
  ROM #(.addrWidth(4), .dataWidth(13)) rom_44 (.addr(t_ff_3_q), .data(out_51), .sel(not_1_out));
  ROM #(.addrWidth(4), .dataWidth(13)) rom_45 (.addr(t_ff_3_q), .data(out_55), .sel(not_1_out));
  ROM #(.addrWidth(4), .dataWidth(13)) rom_46 (.addr(t_ff_3_q), .data(out_60), .sel(not_1_out));
  ROM #(.addrWidth(4), .dataWidth(13)) rom_47 (.addr(t_ff_3_q), .data(out_63), .sel(not_1_out));
  ROM #(.addrWidth(4), .dataWidth(13)) rom_48 (.addr(t_ff_3_q), .data(out_67), .sel(not_1_out));
  ROM #(.addrWidth(4), .dataWidth(13)) rom_49 (.addr(t_ff_3_q), .data(out_70), .sel(not_1_out));
  ROM #(.addrWidth(4), .dataWidth(13)) rom_50 (.addr(t_ff_3_q), .data(out_74), .sel(not_1_out));
  assign controlled_buffer_1_out = not_1_out ? out_38 : 13'bz;  // Controlled_Buffer controlled_buffer_14
  assign controlled_buffer_2_out = not_1_out ? out_42 : 13'bz;  // Controlled_Buffer controlled_buffer_15
  assign controlled_buffer_3_out = not_1_out ? out_45 : 13'bz;  // Controlled_Buffer controlled_buffer_16
  assign controlled_buffer_4_out = not_1_out ? out_48 : 13'bz;  // Controlled_Buffer controlled_buffer_17
  assign controlled_buffer_5_out = not_1_out ? out_51 : 13'bz;  // Controlled_Buffer controlled_buffer_18
  assign controlled_buffer_19_out = not_1_out ? out_55 : 13'bz;  // Controlled_Buffer controlled_buffer_19
  assign controlled_buffer_20_out = not_1_out ? out_60 : 13'bz;  // Controlled_Buffer controlled_buffer_20
  assign controlled_buffer_21_out = not_1_out ? out_63 : 13'bz;  // Controlled_Buffer controlled_buffer_21
  assign controlled_buffer_22_out = not_1_out ? out_67 : 13'bz;  // Controlled_Buffer controlled_buffer_22
  DotMatrix #(.matrixcols(13), .matrixrows(13)) dotmatrix_4 (
    .col0(controlled_buffer_1_out), .col1(controlled_buffer_2_out), .col2(controlled_buffer_3_out),
    .col3(controlled_buffer_4_out), .col4(controlled_buffer_5_out), .col5(controlled_buffer_19_out),
    .col6(controlled_buffer_20_out), .col7(controlled_buffer_21_out), .col8(controlled_buffer_22_out),
    .col9(controlled_buffer_23_out), .col10(controlled_buffer_24_out), .col11(controlled_buffer_25_out),
    .col12(controlled_buffer_26_out));
  assign controlled_buffer_23_out = not_1_out ? out_70 : 13'bz;  // Controlled_Buffer controlled_buffer_23
  assign controlled_buffer_24_out = not_1_out ? out_74 : 13'bz;  // Controlled_Buffer controlled_buffer_24
  assign controlled_buffer_25_out = not_1_out ? out_71 : 13'bz;  // Controlled_Buffer controlled_buffer_25
  assign controlled_buffer_26_out = not_1_out ? out_57 : 13'bz;  // Controlled_Buffer controlled_buffer_26
  ROM #(.addrWidth(4), .dataWidth(13)) rom_51 (.addr(t_ff_3_q), .data(out_57), .sel(not_1_out));
  ROM #(.addrWidth(4), .dataWidth(13)) rom_52 (.addr(t_ff_3_q), .data(out_71), .sel(not_1_out));

  // Notes on the sheet:
  //   contents of rom_1 (hex, n*v repeats v):
  //   1 1 1 1f88 8*0 4*1
  //   contents of rom_2 (hex, n*v repeats v):
  //   0 1 1 888 8*0 4*1
  //   contents of rom_3 (hex, n*v repeats v):
  //   1f8 1 1 888 8*0 4*1
  //   contents of rom_4 (hex, n*v repeats v):
  //   204 1 1 888 8*0 4*1
  //   contents of rom_5 (hex, n*v repeats v):
  //   2d4 1 1 888 8*0 4*1
  //   contents of rom_6 (hex, n*v repeats v):
  //   204 1 1 888 8*0 4*1
  //   contents of rom_7 (hex, n*v repeats v):
  //   2c4 1 1 888 8*0 4*1
  //   contents of rom_8 (hex, n*v repeats v):
  //   204 1 1 888 8*0 4*1
  //   contents of rom_9 (hex, n*v repeats v):
  //   204 1 1 888 8*0 4*1
  //   contents of rom_10 (hex, n*v repeats v):
  //   1f8 1 1 888 8*0 4*1
  //   contents of rom_11 (hex, n*v repeats v):
  //   0 1 1 888 8*0 4*1
  //   contents of rom_12 (hex, n*v repeats v):
  //   8*0 1 1 0 0 4*1
  //   contents of rom_13 (hex, n*v repeats v):
  //   4*0 1f 1f 0 0 3 3 0 0 4*1
  //   contents of rom_14 (hex, n*v repeats v):
  //   1f8 f8 1c 1c 75 75 0 0 3 3 0 0 4*1
  //   contents of rom_15 (hex, n*v repeats v):
  //   204 104 24 24 9b 9b 0 0 3 3 0 0 4*1
  //   contents of rom_16 (hex, n*v repeats v):
  //   2d4 154 54 44 155 155 0 0 7f 7f 0 0 4*1
  //   contents of rom_17 (hex, n*v repeats v):
  //   204 104 44 54 15b 15b 0 0 83 83 0 0 4*1
  //   contents of rom_18 (hex, n*v repeats v):
  //   2c4 144 54 44 115 115 0 0 483 483 0 0 4*1
  //   contents of rom_19 (hex, n*v repeats v):
  //   204 104 44 54 15b 15b 0 0 f83 f83 0 0 4*1
  //   contents of rom_20 (hex, n*v repeats v):
  //   204 104 24 24 155 155 0 0 483 483 0 0 4*1
  //   contents of rom_21 (hex, n*v repeats v):
  //   1f8 f8 1c 1c 9b 9b 0 0 83 83 0 0 4*1
  //   contents of rom_22 (hex, n*v repeats v):
  //   4*0 1375 75 0 0 7f 7f 0 0 4*1
  //   contents of rom_23 (hex, n*v repeats v):
  //   0 1 1 888 8*0 4*1
  //   contents of rom_24 (hex, n*v repeats v):
  //   0 1 1 888 8*0 4*1
  //   contents of rom_25 (hex, n*v repeats v):
  //   8*0 1 1 0 0 4*1
  //   contents of rom_26 (hex, n*v repeats v):
  //   4*0 1f 1f 0 0 3 3 0 0 4*1
  //   contents of rom_27 (hex, n*v repeats v):
  //   1f8 f8 1c 1c 75 75 0 0 3 3 0 0 4*1
  //   contents of rom_28 (hex, n*v repeats v):
  //   204 104 24 24 9b 9b 0 0 3 3 0 0 4*1
  //   contents of rom_29 (hex, n*v repeats v):
  //   2d4 154 54 44 155 155 0 0 7f 7f 0 0 4*1
  //   contents of rom_30 (hex, n*v repeats v):
  //   204 104 44 54 15b 15b 0 0 83 83 0 0 4*1
  //   contents of rom_31 (hex, n*v repeats v):
  //   2c4 144 54 44 115 115 0 0 483 483 0 0 4*1
  //   contents of rom_32 (hex, n*v repeats v):
  //   204 104 44 54 15b 15b 0 0 f83 f83 0 0 4*1
  //   contents of rom_33 (hex, n*v repeats v):
  //   204 104 24 24 155 155 0 0 483 483 0 0 4*1
  //   contents of rom_34 (hex, n*v repeats v):
  //   1f8 f8 1c 1c 9b 9b 0 0 83 83 0 0 4*1
  //   contents of rom_35 (hex, n*v repeats v):
  //   4*0 1375 75 0 0 7f 7f 0 0 4*1
  //   contents of rom_36 (hex, n*v repeats v):
  //   4*0 1900 0 0 0 1 1 0 0 4*1
  //   contents of rom_37 (hex, n*v repeats v):
  //   4*0 151f 1f 0 0 3 3 0 0 4*1
  //   contents of rom_38 (hex, n*v repeats v):
  //   4*0 151f 1f 0 0 3 3 0 0 4*1
  //   contents of rom_39 (hex, n*v repeats v):
  //   4*0 1900 0 0 0 1 1 0 0 4*1
  //   contents of rom_40 (hex, n*v repeats v):
  //   8*0 1 1 0 0 4*1
  //   contents of rom_41 (hex, n*v repeats v):
  //   4*0 1f 1f 0 0 3 3 0 0 4*1
  //   contents of rom_42 (hex, n*v repeats v):
  //   1f8 f8 1c 1c 75 75 0 0 3 3 0 0 4*1
  //   contents of rom_43 (hex, n*v repeats v):
  //   204 104 24 24 9b 9b 0 0 3 3 0 0 4*1
  //   contents of rom_44 (hex, n*v repeats v):
  //   2d4 154 54 44 155 155 0 0 7f 7f 0 0 4*1
  //   contents of rom_45 (hex, n*v repeats v):
  //   204 104 44 54 15b 15b 0 0 83 83 0 0 4*1
  //   contents of rom_46 (hex, n*v repeats v):
  //   2c4 144 54 44 115 115 0 0 483 483 0 0 4*1
  //   contents of rom_47 (hex, n*v repeats v):
  //   204 104 44 54 15b 15b 0 0 f83 f83 0 0 4*1
  //   contents of rom_48 (hex, n*v repeats v):
  //   204 104 24 24 155 155 0 0 483 483 0 0 4*1
  //   contents of rom_49 (hex, n*v repeats v):
  //   1f8 f8 1c 1c 9b 9b 0 0 83 83 0 0 4*1
  //   contents of rom_50 (hex, n*v repeats v):
  //   4*0 1375 75 0 0 7f 7f 0 0 4*1
  //   contents of rom_51 (hex, n*v repeats v):
  //   4*0 1900 0 0 0 1 1 0 0 4*1
  //   contents of rom_52 (hex, n*v repeats v):
  //   4*0 151f 1f 0 0 3 3 0 0 4*1
endmodule

module testes_rom (
  input  in_1,
  input  in_2,
  input  in_3,
  input  in_4,
  output [12:0] out_5,
  output [12:0] out_6,
  output [12:0] out_7,
  output [12:0] out_8,
  output [12:0] out_9,
  output [12:0] out_10,
  output [12:0] out_11,
  output [12:0] out_12,
  output [12:0] out_13,
  output [12:0] out_14,
  output [12:0] out_15,
  output [12:0] out_16,
  output [12:0] out_17
);

  wire clock_1_out, not_1_out;
  wire [1:0] priority_encoder_1_out;
  wire [3:0] t_ff_1_q;
  wire [12:0] rom_1_data, rom_2_data, rom_3_data, rom_4_data, rom_5_data, rom_6_data, rom_7_data, rom_8_data,
       rom_9_data, rom_10_data, rom_11_data, rom_12_data, rom_13_data;

  Clock #(.highDuration(2), .lowDuration(2)) clock_1 (.out(clock_1_out));
  T_Flip_Flop t_ff_1 (.clk(clock_1_out), .T(1'b1), .Q(t_ff_1_q[0]));  // open: Qn, preset, reset, en
  Demultiplexer #(.select(2)) demultiplexer_1 (
    .out1(t_ff_1_q[1]), .out2(t_ff_1_q[2]), .out3(t_ff_1_q[3]), .in(1'b1), .sel(priority_encoder_1_out));  // open: out0, en
  Priority_Encoder #(.select(2), .disabled(0)) priority_encoder_1 (
    .in0(1'b1), .in1(in_1), .in2(in_2), .in3(in_3), .out(priority_encoder_1_out));  // open: gs, en_out, en_in
  ROM #(.addrWidth(4), .dataWidth(13)) rom_1 (.addr(t_ff_1_q), .data(rom_1_data), .sel(in_4));
  ROM #(.addrWidth(4), .dataWidth(13)) rom_2 (.addr(t_ff_1_q), .data(rom_2_data), .sel(in_4));
  ROM #(.addrWidth(4), .dataWidth(13)) rom_3 (.addr(t_ff_1_q), .data(rom_3_data), .sel(in_4));
  ROM #(.addrWidth(4), .dataWidth(13)) rom_4 (.addr(t_ff_1_q), .data(rom_4_data), .sel(in_4));
  ROM #(.addrWidth(4), .dataWidth(13)) rom_5 (.addr(t_ff_1_q), .data(rom_5_data), .sel(in_4));
  ROM #(.addrWidth(4), .dataWidth(13)) rom_6 (.addr(t_ff_1_q), .data(rom_6_data), .sel(in_4));
  ROM #(.addrWidth(4), .dataWidth(13)) rom_7 (.addr(t_ff_1_q), .data(rom_7_data), .sel(in_4));
  ROM #(.addrWidth(4), .dataWidth(13)) rom_8 (.addr(t_ff_1_q), .data(rom_8_data), .sel(in_4));
  ROM #(.addrWidth(4), .dataWidth(13)) rom_9 (.addr(t_ff_1_q), .data(rom_9_data), .sel(in_4));
  ROM #(.addrWidth(4), .dataWidth(13)) rom_10 (.addr(t_ff_1_q), .data(rom_10_data), .sel(in_4));
  ROM #(.addrWidth(4), .dataWidth(13)) rom_11 (.addr(t_ff_1_q), .data(rom_11_data), .sel(in_4));
  assign out_5 = in_4 ? rom_1_data : 13'bz;  // Controlled_Buffer controlled_buffer_1
  assign out_6 = in_4 ? rom_2_data : 13'bz;  // Controlled_Buffer controlled_buffer_2
  assign out_7 = in_4 ? rom_3_data : 13'bz;  // Controlled_Buffer controlled_buffer_3
  assign out_8 = in_4 ? rom_4_data : 13'bz;  // Controlled_Buffer controlled_buffer_4
  assign out_9 = in_4 ? rom_5_data : 13'bz;  // Controlled_Buffer controlled_buffer_5
  assign out_10 = in_4 ? rom_6_data : 13'bz;  // Controlled_Buffer controlled_buffer_6
  assign out_11 = in_4 ? rom_7_data : 13'bz;  // Controlled_Buffer controlled_buffer_7
  assign out_12 = in_4 ? rom_8_data : 13'bz;  // Controlled_Buffer controlled_buffer_8
  assign out_13 = in_4 ? rom_9_data : 13'bz;  // Controlled_Buffer controlled_buffer_9
  DotMatrix #(.matrixcols(13), .matrixrows(13)) dotmatrix_1 (
    .col0(out_5), .col1(out_6), .col2(out_7), .col3(out_8), .col4(out_9), .col5(out_10), .col6(out_11),
    .col7(out_12), .col8(out_13), .col9(out_14), .col10(out_15), .col11(out_16), .col12(out_17));
  assign out_14 = in_4 ? rom_10_data : 13'bz;  // Controlled_Buffer controlled_buffer_10
  assign out_15 = in_4 ? rom_11_data : 13'bz;  // Controlled_Buffer controlled_buffer_11
  assign out_16 = in_4 ? rom_13_data : 13'bz;  // Controlled_Buffer controlled_buffer_12
  assign out_17 = in_4 ? rom_12_data : 13'bz;  // Controlled_Buffer controlled_buffer_13
  ROM #(.addrWidth(4), .dataWidth(13)) rom_12 (.addr(t_ff_1_q), .data(rom_12_data), .sel(in_4));
  ROM #(.addrWidth(4), .dataWidth(13)) rom_13 (.addr(t_ff_1_q), .data(rom_13_data), .sel(in_4));
  not not_1 (not_1_out, in_4);

  // Notes on the sheet:
  //   contents of rom_1 (hex, n*v repeats v):
  //   8*0 1 1 0 0 4*1
  //   contents of rom_2 (hex, n*v repeats v):
  //   4*0 1f 1f 0 0 3 3 0 0 4*1
  //   contents of rom_3 (hex, n*v repeats v):
  //   1f8 f8 1c 1c 75 75 0 0 3 3 0 0 4*1
  //   contents of rom_4 (hex, n*v repeats v):
  //   204 104 24 24 9b 9b 0 0 3 3 0 0 4*1
  //   contents of rom_5 (hex, n*v repeats v):
  //   2d4 154 54 44 155 155 0 0 7f 7f 0 0 4*1
  //   contents of rom_6 (hex, n*v repeats v):
  //   204 104 44 54 15b 15b 0 0 83 83 0 0 4*1
  //   contents of rom_7 (hex, n*v repeats v):
  //   2c4 144 54 44 115 115 0 0 483 483 0 0 4*1
  //   contents of rom_8 (hex, n*v repeats v):
  //   204 104 44 54 15b 15b 0 0 f83 f83 0 0 4*1
  //   contents of rom_9 (hex, n*v repeats v):
  //   204 104 24 24 155 155 0 0 483 483 0 0 4*1
  //   contents of rom_10 (hex, n*v repeats v):
  //   1f8 f8 1c 1c 9b 9b 0 0 83 83 0 0 4*1
  //   contents of rom_11 (hex, n*v repeats v):
  //   4*0 1375 75 0 0 7f 7f 0 0 4*1
  //   contents of rom_12 (hex, n*v repeats v):
  //   4*0 1900 0 0 0 1 1 0 0 4*1
  //   contents of rom_13 (hex, n*v repeats v):
  //   4*0 151f 1f 0 0 3 3 0 0 4*1
endmodule

module \funções_mais_lentas  (
  input  in_1,
  input  in_2,
  input  in_3,
  output out_4,
  output out_5,
  output out_6,
  output out_7,
  output out_8,
  output out_9,
  output out_10
);

  wire and_1_out, and_2_out, and_3_out, and_4_out, and_5_out, and_6_out, and_7_out, and_8_out, and_9_out,
       and_10_out, and_11_out, and_12_out, and_13_out, and_14_out, and_15_out, and_16_out, and_17_out,
       and_18_out, and_19_out, and_20_out, and_21_out, and_22_out, and_23_out, and_24_out, and_25_out,
       and_26_out, and_27_out, and_28_out, and_29_out, and_31_out, and_32_out, and_34_out, clock_1_out,
       d_ff_1_q, d_ff_2_q, d_ff_3_q, d_ff_4_q, d_ff_5_q, d_ff_6_q, d_ff_7_q, not_1_out, not_2_out, not_3_out,
       not_4_out, not_5_out, not_6_out, not_7_out, not_8_out, not_9_out, not_10_out, not_11_out, not_12_out,
       not_13_out, not_14_out, or_1_out, or_2_out, or_3_out, or_4_out, or_5_out, or_6_out, or_7_out,
       or_8_out, or_9_out, t_ff_1_qn, t_ff_2_qn, t_ff_3_qn, t_ff_4_qn, t_ff_5_qn, xor_1_out, xor_2_out,
       xor_3_out, xor_4_out, xor_5_out, xor_6_out, xor_7_out, xor_8_out, xor_9_out;

  Clock #(.highDuration(2)) clock_1 (.out(clock_1_out));
  not not_1 (not_1_out, d_ff_1_q);
  and and_1 (and_1_out, not_14_out, in_3);
  T_Flip_Flop t_ff_1 (
    .clk(clock_1_out), .T(1'b1), .Q(out_4), .Qn(t_ff_1_qn), .preset(or_1_out), .reset(and_3_out),
    .en(and_32_out));
  or or_1 (or_1_out, in_1, d_ff_7_q, and_2_out);
  and and_2 (and_2_out, d_ff_1_q, and_1_out);
  and and_3 (and_3_out, not_1_out, not_1_out, and_1_out);
  and and_4 (and_4_out, 1'b1, out_4);
  D_Flip_Flop d_ff_1 (.clk(and_1_out), .D(xor_1_out), .Q(d_ff_1_q), .en(not_14_out));  // open: Qn, preset, reset
  xor xor_1 (xor_1_out, out_4, 1'b1);
  T_Flip_Flop t_ff_2 (
    .clk(clock_1_out), .T(t_ff_1_qn), .Q(out_5), .Qn(t_ff_2_qn), .preset(or_2_out), .reset(and_6_out),
    .en(and_32_out));
  or or_2 (or_2_out, d_ff_7_q, in_1, and_5_out);
  and and_5 (and_5_out, d_ff_2_q, and_1_out);
  not not_2 (not_2_out, d_ff_2_q);
  and and_6 (and_6_out, not_2_out, not_2_out, and_1_out);
  and and_7 (and_7_out, t_ff_1_qn, t_ff_2_qn);
  or or_3 (or_3_out, d_ff_7_q, and_8_out, in_1);
  and and_8 (and_8_out, d_ff_3_q, and_1_out);
  not not_3 (not_3_out, d_ff_3_q);
  xor xor_2 (xor_2_out, 1'b1, and_4_out);
  and and_9 (and_9_out, 1'b1, and_4_out);
  and and_10 (and_10_out, 1'b1, out_5);
  and and_11 (and_11_out, out_5, and_4_out);
  xor xor_3 (xor_3_out, 1'b1, or_5_out);
  and and_12 (and_12_out, 1'b1, or_5_out);
  and and_13 (and_13_out, 1'b1, out_6);
  and and_14 (and_14_out, out_6, or_5_out);
  T_Flip_Flop t_ff_3 (
    .clk(clock_1_out), .T(and_7_out), .Q(out_6), .Qn(t_ff_3_qn), .preset(or_3_out), .reset(and_15_out),
    .en(and_32_out));
  and and_15 (and_15_out, not_3_out, not_3_out, and_1_out);
  and and_16 (and_16_out, and_7_out, t_ff_3_qn);
  or or_4 (or_4_out, d_ff_7_q, in_1, and_17_out);
  or or_5 (or_5_out, and_9_out, and_10_out, and_11_out);
  or or_6 (or_6_out, and_12_out, and_13_out, and_14_out);
  T_Flip_Flop t_ff_4 (
    .clk(clock_1_out), .T(and_16_out), .Q(out_7), .Qn(t_ff_4_qn), .preset(or_4_out), .reset(and_18_out),
    .en(and_32_out));
  and and_17 (and_17_out, d_ff_4_q, and_1_out);
  not not_4 (not_4_out, d_ff_4_q);
  and and_18 (and_18_out, not_4_out, not_4_out, and_1_out);
  D_Flip_Flop d_ff_2 (.clk(and_1_out), .D(xor_4_out), .Q(d_ff_2_q), .en(not_14_out));  // open: Qn, preset, reset
  xor xor_4 (xor_4_out, out_5, xor_2_out);
  xor xor_5 (xor_5_out, out_6, xor_3_out);
  and and_19 (and_19_out, and_16_out, t_ff_4_qn);
  D_Flip_Flop d_ff_3 (.clk(and_1_out), .D(xor_5_out), .Q(d_ff_3_q), .en(not_14_out));  // open: Qn, preset, reset
  or or_7 (or_7_out, d_ff_7_q, in_1, and_20_out);
  T_Flip_Flop t_ff_5 (
    .clk(clock_1_out), .T(and_19_out), .Q(out_8), .Qn(t_ff_5_qn), .preset(or_7_out), .reset(and_21_out),
    .en(and_32_out));
  and and_20 (and_20_out, d_ff_5_q, and_1_out);
  not not_5 (not_5_out, d_ff_5_q);
  and and_21 (and_21_out, not_5_out, not_5_out, and_1_out);
  xor xor_6 (xor_6_out, 1'b1, or_6_out);
  and and_22 (and_22_out, 1'b1, or_6_out);
  and and_23 (and_23_out, 1'b1, out_7);
  and and_24 (and_24_out, out_7, or_6_out);
  or or_8 (or_8_out, d_ff_7_q, in_1, and_26_out);
  T_Flip_Flop t_ff_6 (
    .clk(clock_1_out), .T(and_25_out), .Q(out_9), .preset(or_8_out), .reset(and_27_out), .en(and_32_out));  // open: Qn
  and and_25 (and_25_out, and_19_out, t_ff_5_qn);
  and and_26 (and_26_out, d_ff_6_q, and_1_out);
  not not_6 (not_6_out, d_ff_6_q);
  xor xor_7 (xor_7_out, out_7, xor_6_out);
  or or_9 (or_9_out, and_22_out, and_23_out, and_24_out);
  and and_27 (and_27_out, not_6_out, not_6_out, and_1_out);
  D_Flip_Flop d_ff_4 (.clk(and_1_out), .D(xor_7_out), .Q(d_ff_4_q), .en(not_14_out));  // open: Qn, preset, reset
  // Probe on {out_9, out_8, out_7, out_6, out_5, out_4}
  and and_28 (and_28_out, out_9, and_29_out);
  xor xor_8 (xor_8_out, out_8, or_9_out);
  and and_29 (and_29_out, or_9_out, out_8);
  not not_7 (not_7_out, out_4);
  not not_8 (not_8_out, out_5);
  not not_9 (not_9_out, out_6);
  not not_10 (not_10_out, out_7);
  not not_11 (not_11_out, out_8);
  not not_12 (not_12_out, out_9);
  xor xor_9 (xor_9_out, and_29_out, out_9);
  D_Flip_Flop d_ff_5 (.clk(and_1_out), .D(xor_8_out), .Q(d_ff_5_q), .en(not_14_out));  // open: Qn, preset, reset
  and and_30 (out_10, not_9_out, not_7_out, not_8_out, not_10_out, not_11_out, not_12_out);
  and and_31 (and_31_out, out_4, out_5, out_6, out_7, out_9, out_8);
  D_Flip_Flop d_ff_6 (.clk(and_1_out), .D(xor_9_out), .Q(d_ff_6_q), .en(not_14_out));  // open: Qn, preset, reset
  and and_32 (and_32_out, in_2, not_13_out);
  not not_13 (not_13_out, out_10);
  // AND_Gate and_33 has open pins: in0=xor_9_out, in1=xor_8_out, in2=xor_7_out, in4=xor_5_out, in5=xor_4_out, in6=xor_1_out, out=open
  and and_34 (and_34_out, and_28_out, and_31_out);
  not not_14 (not_14_out, and_34_out);
  D_Flip_Flop d_ff_7 (.clk(and_1_out), .D(and_28_out), .Q(d_ff_7_q), .reset(and_31_out));  // open: Qn, preset, en
endmodule
